# Fritzing sketch flow test (saved by Fritzing 0.9.3b)
breadboards: 1

parts:
  Raspberry_Pi_1 = Raspberry Pi 3 [part_number=RPI-3-V1.2]
  YF-S201_Flow_Meter1 = YF-S201 Water Flow Meter
  R1 = Resistor [tolerance=±5% resistance=220 package="0805 [SMD]"]
  R2 = Resistor [tolerance=±5% resistance=220 package="0805 [SMD]"]

nets:
  N1: Raspberry_Pi_1.GIPO27, R1.Pin_0, R2.Pin_1
  GND: Raspberry_Pi_1.GND, YF-S201_Flow_Meter1.GND, R1.Pin_1
  5V: Raspberry_Pi_1.5V, YF-S201_Flow_Meter1.VCC

notes:
  4.7k 10k

custom parts:
  YF-S201 Water Flow Meter: The YF-S201 Flow Meter. The input voltage is 5V to 24V (DC).
