# Fritzing sketch température modele (saved by Fritzing 0.9.3b)
breadboards: 1

parts:
  R1 = Resistor [tolerance=±5% resistance=220 package=THT]
  Composant1 = Arduino Uno (Rev3) - ICSP
  DS1 = DS18B20 1-Wire Temperature Sensor [part_number=DS18B20]

nets:
  N1: R1.Pin_0, Composant1.A0, DS1.DQ
  5V: R1.Pin_1, Composant1.5V, DS1.VDD
  GND: Composant1.GND, DS1.GND
